# Fritzing sketch clocks (saved by Fritzing 1.0.1rc)
perfboards: 1

parts:
  V1 = DC Power [voltage=5]  # not connected
  S1 = Pushbutton [package=THT]  # not connected
  R1 = Photocell (LDR) [power=0.25W dark_resistance_@0.01lx=300kΩ light_resistance_@100lx=400Ω luminance=10lx package=THT]  # not connected
  ZS-042_RTC1 = ZS-042 RTC Module
  M1 = RioRand LM2596
  Grove1 = Grove 4 Digit Display
  Part1 = Digital Temperature Sensor Breakout - TMP102

nets:
  N1: ZS-042_RTC1.VCC, M1.Pin_3, Part1.V+
  N2: ZS-042_RTC1.SDA, Part1.SDA
  N3: ZS-042_RTC1.SCL, Part1.SCL
  N4: M1.Pin_4, Grove1.CLK

notes:
  Reset button
  ESP32 C3 WeAct
  USB C
  BME680 Temperature sensor
  DS3231 RTL Clocks
  LM2596 DC-DC Step Down
  12V Power source
  Light sensor breakout board
  TM1637 display
